// Logisim project Project3Given (2) (2).circ as structural Verilog: 9 circuits, main circuit CPU15
module main (
  input  EnableBreakpoint,
  input  [14:0] Breakpoint
);

  wire and_2_out, and_3_out, chipset_1_irq, CLK, clock_1_out, cpu15_1_c, cpu15_1_e, cpu15_1_i, cpu15_1_n,
       cpu15_1_o, cpu15_1_z, KBCLR, KBIRQ, KBRD, MEMCS, nand_1_out, RE, TTYCLR, TTYWE, WE;
  wire [6:0] KBDATA, TTYDATA;
  wire [7:0] cpu15_1_srf;
  wire [14:0] ADDR, chipset_1_ivect, chipset_1_led0, chipset_1_led1, chipset_1_led2, chipset_1_led3,
       chipset_1_led4, chipset_1_led5, chipset_1_led6, chipset_1_led7, chipset_1_led8, chipset_1_led9,
       chipset_1_leda, chipset_1_ledb, chipset_1_ledc, chipset_1_ledd, chipset_1_lede, cpu15_1_ib,
       cpu15_1_pc, cpu15_1_r0, cpu15_1_r1, cpu15_1_r2, cpu15_1_r3, cpu15_1_r4, cpu15_1_r5, cpu15_1_r6,
       cpu15_1_r7, cpu15_1_srp, DATA, xnor_1_out;

  Clock clock_1 (.out(clock_1_out));
  nand nand_1 (nand_1_out, EnableBreakpoint, xnor_1_out[0], xnor_1_out[1], xnor_1_out[2], xnor_1_out[3], xnor_1_out[4], xnor_1_out[5], xnor_1_out[6], xnor_1_out[7], xnor_1_out[8], xnor_1_out[9], xnor_1_out[10], xnor_1_out[11], xnor_1_out[12], xnor_1_out[13], xnor_1_out[14], 1'b1);
  and and_1 (CLK, clock_1_out, nand_1_out);
  assign xnor_1_out = ~(Breakpoint ^ cpu15_1_pc);  // XNOR_Gate xnor_1, 15 bits wide
  LED I (.in(cpu15_1_i));
  LED Z (.in(cpu15_1_z));
  LED N (.in(cpu15_1_n));
  LED O (.in(cpu15_1_o));
  LED C (.in(cpu15_1_c));
  LED E (.in(cpu15_1_e));
  and and_2 (and_2_out, WE, MEMCS);
  and and_3 (and_3_out, MEMCS, RE);
  RAM #(.addrWidth(15), .asyncread("true"), .dataWidth(15), .databus("bidir")) ram_1 (
    .addr(ADDR), .we(and_2_out), .oe(and_3_out), .clk(CLK));  // open: data
  // Probe on cpu15_1_pc
  // Probe on cpu15_1_ib
  // Probe on cpu15_1_srp
  // Probe on cpu15_1_srf
  // Probe on cpu15_1_r0
  // Probe on cpu15_1_r1
  // Probe on cpu15_1_r2
  // Probe on cpu15_1_r3
  // Probe on cpu15_1_r4
  // Probe on cpu15_1_r5
  // Probe on cpu15_1_r6
  // Probe on cpu15_1_r7
  CPU15 cpu15_1 (
    .I(cpu15_1_i), .Z(cpu15_1_z), .N(cpu15_1_n), .O(cpu15_1_o), .C(cpu15_1_c), .E(cpu15_1_e),
    .PC(cpu15_1_pc), .IB(cpu15_1_ib), .SRP(cpu15_1_srp), .SRF(cpu15_1_srf), .R0(cpu15_1_r0), .R1(cpu15_1_r1),
    .R2(cpu15_1_r2), .R3(cpu15_1_r3), .R4(cpu15_1_r4), .R5(cpu15_1_r5), .R6(cpu15_1_r6), .R7(cpu15_1_r7),
    .CLK(CLK), .IRQ(chipset_1_irq), .RE(RE), .WE(WE), .ADDR(ADDR), .DATAIN(DATA), .DATAOUT(DATA));
  // Probe on ADDR
  // Probe on DATA
  // Probe on chipset_1_ivect
  // Probe on TTYDATA
  CHIPSET chipset_1 (
    .RE(RE), .WE(WE), .ADDR(ADDR), .CPUDATAIN(DATA), .CPUDATAOUT(DATA), .IRQ(chipset_1_irq),
    .IVECT(chipset_1_ivect), .CLK(CLK), .MEMCS(MEMCS), .TTYWR(TTYWE), .TTYCLR(TTYCLR), .TTYDATA(TTYDATA),
    .KBRD(KBRD), .KBCLR(KBCLR), .KBIRQ(KBIRQ), .KBDATA(KBDATA), .LED0(chipset_1_led0), .LED1(chipset_1_led1),
    .LED2(chipset_1_led2), .LED3(chipset_1_led3), .LED4(chipset_1_led4), .LED5(chipset_1_led5),
    .LED6(chipset_1_led6), .LED7(chipset_1_led7), .LED8(chipset_1_led8), .LED9(chipset_1_led9),
    .LEDA(chipset_1_leda), .LEDB(chipset_1_ledb), .LEDC(chipset_1_ledc), .LEDD(chipset_1_ledd),
    .LEDE(chipset_1_lede));
  TTY tty_1 (.data(TTYDATA), .clk(CLK), .we(TTYWE), .clr(TTYCLR));
  Keyboard keyboard_1 (.clk(CLK), .re(KBRD), .clr(KBCLR), .avail(KBIRQ), .data(KBDATA));
  DotMatrix #(.matrixcols(15), .matrixrows(15)) dotmatrix_1 (
    .col0(chipset_1_led0), .col1(chipset_1_led1), .col2(chipset_1_led2), .col3(chipset_1_led3),
    .col4(chipset_1_led4), .col5(chipset_1_led5), .col6(chipset_1_led6), .col7(chipset_1_led7),
    .col8(chipset_1_led8), .col9(chipset_1_led9), .col10(chipset_1_leda), .col11(chipset_1_ledb),
    .col12(chipset_1_ledc), .col13(chipset_1_ledd), .col14(chipset_1_lede));
endmodule

// CPU
module CPU15 (
  input  [14:0] DATAIN,
  input  CLK,
  input  IRQ,
  output [14:0] PC,
  output [14:0] IB,
  output [14:0] SRP,
  output [7:0] SRF,
  output [14:0] R0,
  output [14:0] R1,
  output [14:0] R2,
  output [14:0] R3,
  output [14:0] R4,
  output [14:0] R5,
  output [14:0] R6,
  output [14:0] R7,
  output RE,
  output WE,
  output I,
  output Z,
  output [14:0] ADDR,
  output N,
  output O,
  output C,
  output E,
  output [14:0] DATAOUT
);

  wire Execute_Writeback, Fetch_Decode, W;
  wire [1:0] ASel, BSel;
  wire [2:0] ALUOP;
  wire [3:0] NF;
  wire [7:0] WM;
  wire [7:4] F;
  wire [14:0] A, adder15_1_s, B, D, Prev_PC;

  Counter #(.max('h1), .width(1)) counter_1 (.Q(Execute_Writeback), .clk(CLK));  // open: load, D, count, carry, up, clr
  DECODE15 decode15_1 (
    .OPCODE(DATAIN[4:0]), .ASEL(ASel), .BSEL(BSel), .ALUOP(ALUOP), .REGW(W), .FLAGWM(WM));  // open: SWI, STORE, LOAD, REGDATASRC, FLAGSRC, SRPW, SRFW
  REGS15 regs15_1 (
    .D(D), .W(W), .SelD(IB[7:5]), .CLK(CLK), .SelA(IB[10:8]), .SelB(IB[13:11]), .R0(R0), .R1(R1), .R2(R2),
    .R3(R3), .R4(R4), .R5(R5), .R6(R6), .R7(R7), .A(A), .B(B));
  not not_1 (Fetch_Decode, Execute_Writeback);
  IMM15 imm15_1 (.INST(DATAIN), .SEXT(D));
  assign IB = Fetch_Decode ? DATAIN : 15'bz;  // Controlled_Buffer controlled_buffer_1
  assign ADDR = Fetch_Decode ? PC : 15'bz;  // Controlled_Buffer controlled_buffer_2
  ALU15 alu15_1 (.A(A), .B(B), .OP(ALUOP), .CIN(C), .OIN(O), .R(DATAOUT), .C(NF[2]), .O(NF[3]), .N(NF[1]), .Z(NF[0]));
  ADDER15 adder15_1 (.A(Prev_PC), .B(15'h1), .S(adder15_1_s));  // open: CIN, COUT
  Register #(.width(15)) register_1 (.D(PC), .en(Fetch_Decode), .Q(Prev_PC), .clk(CLK));  // open: clr
  FLAGS8 flags8_1 (.NF({4'b0000, NF}), .WM(WM), .CLK(CLK), .IRQ(IRQ), .F({F[7], I, E, F[4], O, C, N, Z}));
  Register #(.width(15)) register_2 (.D(adder15_1_s), .en(Execute_Writeback), .Q(PC), .clk(CLK));  // open: clr

  // Other names for the same wires on the sheet: DATA[14:0] = DATAIN; OP[4:0] = DATAIN[4:0];
  //   F (some bits) = {I, E, O, C, N, Z}; SelD[2:0] = IB[7:5]; SelA[2:0] = IB[10:8]; SelB[2:0] = IB[13:11]
endmodule

module CHIPSET (
  input  RE,
  input  WE,
  input  [14:0] ADDR,
  input  [14:0] CPUDATAIN,
  input  KBIRQ,
  input  [6:0] KBDATA,
  input  CLK,
  output MEMCS,
  output TTYWR,
  output [14:0] IVECT,
  output TTYCLR,
  output [6:0] TTYDATA,
  output KBRD,
  output KBCLR,
  output [14:0] CPUDATAOUT,
  output IRQ,
  output [14:0] LED0,
  output [14:0] LED1,
  output [14:0] LED2,
  output [14:0] LED3,
  output [14:0] LED4,
  output [14:0] LED5,
  output [14:0] LED6,
  output [14:0] LED7,
  output [14:0] LED8,
  output [14:0] LED9,
  output [14:0] LEDA,
  output [14:0] LEDB,
  output [14:0] LEDC,
  output [14:0] LEDD,
  output [14:0] LEDE
);

  wire and_1_out, and_8_out, and_10_out, DATA7, IOCS, IVECTADDR, IVECTEN, IVECTRE, KBCS, LED0EN, LED0END,
       LED1EN, LED1END, LED2EN, LED2END, LED3EN, LED3END, LED4EN, LED4END, LED5EN, LED5END, LED6EN, LED6END,
       LED7EN, LED7END, LED8EN, LED8END, LED9EN, LED9END, LEDAEN, LEDAEND, LEDBEN, LEDBEND, LEDCEN, LEDCEND,
       LEDCS, LEDDEN, LEDDEND, LEDEEN, LEDEEND, LEDFEND, LEDRE, multiplexer_17_out, multiplexer_18_out, RWE,
       TTYCS;
  wire [14:0] DATAL0, DATAL1, DATAL2, DATAL3, DATAL4, DATAL5, DATAL6, DATAL7, DATAL8, DATAL9, DATALA, DATALB,
       DATALC, DATALD, DATALE, LEDDATA;
  wire [14:8] KBDATA15;

  assign CPUDATAOUT = KBRD ? {KBDATA15, DATA7, KBDATA} : 15'bz;  // Controlled_Buffer controlled_buffer_1
  assign CPUDATAOUT = LEDRE ? LEDDATA : 15'bz;  // Controlled_Buffer controlled_buffer_2
  assign CPUDATAOUT = IVECTRE ? IVECT : 15'bz;  // Controlled_Buffer controlled_buffer_3
  Register #(.width(15)) register_1 (.D(DATAL0), .en(LED0EN), .Q(LED0), .clk(CLK));  // open: clr
  Register #(.width(15)) register_2 (.D(DATAL1), .en(LED1EN), .Q(LED1), .clk(CLK));  // open: clr
  Register #(.width(15)) register_3 (.D(DATAL2), .en(LED2EN), .Q(LED2), .clk(CLK));  // open: clr
  Register #(.width(15)) register_4 (.D(DATAL3), .en(LED3EN), .Q(LED3), .clk(CLK));  // open: clr
  Register #(.width(15)) register_5 (.D(DATAL4), .en(LED4EN), .Q(LED4), .clk(CLK));  // open: clr
  and and_1 (and_1_out, WE, LEDCS);
  Decoder #(.select(4)) decoder_1 (
    .out0(LED0END), .out1(LED1END), .out2(LED2END), .out3(LED3END), .out4(LED4END), .out5(LED5END),
    .out6(LED6END), .out7(LED7END), .out8(LED8END), .out9(LED9END), .out10(LEDAEND), .out11(LEDBEND),
    .out12(LEDCEND), .out13(LEDDEND), .out14(LEDEEND), .out15(LEDFEND), .sel(ADDR[3:0]), .en(and_1_out));
  Register #(.width(15)) register_6 (.D(DATAL5), .en(LED5EN), .Q(LED5), .clk(CLK));  // open: clr
  Register #(.width(15)) register_7 (.D(DATAL6), .en(LED6EN), .Q(LED6), .clk(CLK));  // open: clr
  Register #(.width(15)) register_8 (.D(DATAL7), .en(LED7EN), .Q(LED7), .clk(CLK));  // open: clr
  Register #(.width(15)) register_9 (.D(DATAL8), .en(LED8EN), .Q(LED8), .clk(CLK));  // open: clr
  Register #(.width(15)) register_10 (.D(DATAL9), .en(LED9EN), .Q(LED9), .clk(CLK));  // open: clr
  or or_1 (LED0EN, LED0END, LEDFEND);
  or or_2 (LED1EN, LED1END, LEDFEND);
  or or_3 (LED2EN, LED2END, LEDFEND);
  or or_4 (LED3EN, LED3END, LEDFEND);
  or or_5 (LED4EN, LED4END, LEDFEND);
  or or_6 (LED5EN, LED5END, LEDFEND);
  or or_7 (LED6EN, LED6END, LEDFEND);
  or or_8 (LED7EN, LED7END, LEDFEND);
  or or_9 (LED8EN, LED8END, LEDFEND);
  or or_10 (LED9EN, LED9END, LEDFEND);
  or or_11 (LEDAEN, LEDAEND, LEDFEND);
  or or_12 (LEDBEN, LEDBEND, LEDFEND);
  or or_13 (LEDCEN, LEDCEND, LEDFEND);
  or or_14 (LEDDEN, LEDDEND, LEDFEND);
  or or_15 (LEDEEN, LEDEEND, LEDFEND);
  Pull_Resistor pull_resistor_1 (.node(KBDATA15[14]));
  Pull_Resistor pull_resistor_2 (.node(KBDATA15[13]));
  Pull_Resistor pull_resistor_3 (.node(KBDATA15[12]));
  Pull_Resistor pull_resistor_4 (.node(KBDATA15[11]));
  Pull_Resistor pull_resistor_5 (.node(KBDATA15[10]));
  Pull_Resistor pull_resistor_6 (.node(KBDATA15[9]));
  Pull_Resistor pull_resistor_7 (.node(KBDATA15[8]));
  Pull_Resistor pull_resistor_8 (.node(DATA7));
  Register #(.width(15)) register_11 (.D(DATALA), .en(LEDAEN), .Q(LEDA), .clk(CLK));  // open: clr
  Register #(.width(15)) register_12 (.D(DATALB), .en(LEDBEN), .Q(LEDB), .clk(CLK));  // open: clr
  Register #(.width(15)) register_13 (.D(DATALC), .en(LEDCEN), .Q(LEDC), .clk(CLK));  // open: clr
  Register #(.width(15)) register_14 (.D(DATALD), .en(LEDDEN), .Q(LEDD), .clk(CLK));  // open: clr
  Register #(.width(15)) register_15 (.D(DATALE), .en(LEDEEN), .Q(LEDE), .clk(CLK));  // open: clr
  Multiplexer #(.width(15)) multiplexer_1 (.in0(CPUDATAIN), .in1(LED1), .out(DATAL0), .sel(LEDFEND));
  Multiplexer #(.width(15)) multiplexer_2 (.in0(CPUDATAIN), .in1(LED2), .out(DATAL1), .sel(LEDFEND));
  Multiplexer #(.width(15)) multiplexer_3 (.in0(CPUDATAIN), .in1(LED3), .out(DATAL2), .sel(LEDFEND));
  Multiplexer #(.width(15)) multiplexer_4 (.in0(CPUDATAIN), .in1(LED4), .out(DATAL3), .sel(LEDFEND));
  Multiplexer #(.width(15)) multiplexer_5 (.in0(CPUDATAIN), .in1(LED5), .out(DATAL4), .sel(LEDFEND));
  Multiplexer #(.select(4), .width(15)) multiplexer_6 (
    .in0(LED0), .in1(LED1), .in2(LED2), .in3(LED3), .in4(LED4), .in5(LED5), .in6(LED6), .in7(LED7),
    .in8(LED8), .in9(LED9), .in10(LEDA), .in11(LEDB), .in12(LEDC), .in13(LEDD), .in14(LEDE),
    .in15({15{1'b0}}), .out(LEDDATA), .sel(ADDR[3:0]));
  Multiplexer #(.width(15)) multiplexer_7 (.in0(CPUDATAIN), .in1(LED6), .out(DATAL5), .sel(LEDFEND));
  Multiplexer #(.width(15)) multiplexer_8 (.in0(CPUDATAIN), .in1(LED7), .out(DATAL6), .sel(LEDFEND));
  Multiplexer #(.width(15)) multiplexer_9 (.in0(CPUDATAIN), .in1(LED8), .out(DATAL7), .sel(LEDFEND));
  Multiplexer #(.width(15)) multiplexer_10 (.in0(CPUDATAIN), .in1(LED9), .out(DATAL8), .sel(LEDFEND));
  Multiplexer #(.width(15)) multiplexer_11 (.in0(CPUDATAIN), .in1(LEDA), .out(DATAL9), .sel(LEDFEND));
  and and_2 (LEDRE, RE, LEDCS);
  Multiplexer #(.width(15)) multiplexer_12 (.in0(CPUDATAIN), .in1(LEDB), .out(DATALA), .sel(LEDFEND));
  Multiplexer #(.width(15)) multiplexer_13 (.in0(CPUDATAIN), .in1(LEDC), .out(DATALB), .sel(LEDFEND));
  Multiplexer #(.width(15)) multiplexer_14 (.in0(CPUDATAIN), .in1(LEDD), .out(DATALC), .sel(LEDFEND));
  Multiplexer #(.width(15)) multiplexer_15 (.in0(CPUDATAIN), .in1(LEDE), .out(DATALD), .sel(LEDFEND));
  Multiplexer #(.width(15)) multiplexer_16 (.in0(CPUDATAIN), .in1(CPUDATAIN), .out(DATALE), .sel(LEDFEND));
  and and_3 (IOCS, ADDR[5], ADDR[6], ADDR[7], ADDR[8], ADDR[9], ADDR[10], ADDR[11], ADDR[12], ADDR[13], ADDR[14], 1'b1);
  and and_4 (TTYCS, IOCS, ADDR[0], ~ADDR[1], ~ADDR[2], ~ADDR[3], ADDR[4]);  // AND_Gate
  and and_5 (KBCS, IOCS, ~ADDR[0], ~ADDR[1], ~ADDR[2], ~ADDR[3], ADDR[4]);  // AND_Gate
  and and_6 (IVECTADDR, ADDR[0], ADDR[1], ADDR[2], ADDR[3], ADDR[4], ADDR[5], ADDR[6], ADDR[7], ADDR[8], ADDR[9], ADDR[10], ADDR[11], ADDR[12], ADDR[13], ADDR[14]);
  and and_7 (TTYWR, TTYCS, WE);
  and and_8 (and_8_out, TTYWR, DATA7);
  and and_9 (KBRD, KBCS, RE);
  and and_10 (and_10_out, KBCS, WE);
  Multiplexer multiplexer_17 (.in0(and_10_out), .in1(1'b0), .out(multiplexer_17_out), .sel(KBCLR));
  and and_11 (LEDCS, IOCS, ~ADDR[4], RWE);  // AND_Gate
  and and_12 (IVECTEN, IVECTADDR, WE);
  and and_13 (IVECTRE, IVECTADDR, RE);
  or or_16 (RWE, RE, WE);
  and and_14 (MEMCS, ~IOCS, RWE);  // AND_Gate
  Multiplexer multiplexer_18 (.in0(and_8_out), .in1(1'b0), .out(multiplexer_18_out), .sel(TTYCLR));
  D_Flip_Flop d_ff_1 (.clk(CLK), .D(multiplexer_17_out), .Q(KBCLR));  // open: Qn, preset, reset
  Register #(.width(15)) register_16 (.D(CPUDATAIN), .en(IVECTEN), .Q(IVECT), .clk(CLK));  // open: clr
  D_Flip_Flop d_ff_2 (.clk(CLK), .D(multiplexer_18_out), .Q(TTYCLR));  // open: Qn, preset, reset

  assign IRQ = KBIRQ;
  assign TTYDATA = CPUDATAIN[6:0];

  // Other names for the same wires on the sheet: DATA[14:0] = CPUDATAIN; KBDATA15[7:0] = {DATA7, KBDATA}
endmodule

module ADDER15 (
  input  [14:0] A,
  input  [14:0] B,
  input  CIN,
  output COUT,
  output [14:0] S
);

  wire PFin;
  wire [14:0] G, P;

  Adder #(.width(15)) adder_1 (.a(A), .b(B), .out(S), .cin(CIN), .cout(COUT));
  and and_1 (PFin, P[0], P[1], P[2], P[3], P[4], P[5], P[6], P[7], P[9], P[10], P[11], P[12], P[13], P[14], P[8], CIN);
  assign G = A & B;  // AND_Gate and_2, 15 bits wide
  assign P = A | B;  // OR_Gate or_1, 15 bits wide
endmodule

module REGS15 (
  input  [14:0] D,
  input  W,
  input  [2:0] SelD,
  input  CLK,
  input  [2:0] SelA,
  input  [2:0] SelB,
  output [14:0] R0,
  output [14:0] R1,
  output [14:0] R2,
  output [14:0] R3,
  output [14:0] R4,
  output [14:0] R5,
  output [14:0] R6,
  output [14:0] R7,
  output [14:0] A,
  output [14:0] B
);

  wire demultiplexer_2_out0, demultiplexer_2_out1, demultiplexer_2_out2, demultiplexer_2_out3,
       demultiplexer_2_out4, demultiplexer_2_out5, demultiplexer_2_out6, demultiplexer_2_out7;
  wire [14:0] demultiplexer_1_out0, demultiplexer_1_out1, demultiplexer_1_out2, demultiplexer_1_out3,
       demultiplexer_1_out4, demultiplexer_1_out5, demultiplexer_1_out6, demultiplexer_1_out7, register_8_q;

  Demultiplexer #(.select(3), .width(15)) demultiplexer_1 (
    .out0(demultiplexer_1_out0), .out1(demultiplexer_1_out1), .out2(demultiplexer_1_out2),
    .out3(demultiplexer_1_out3), .out4(demultiplexer_1_out4), .out5(demultiplexer_1_out5),
    .out6(demultiplexer_1_out6), .out7(demultiplexer_1_out7), .in(D), .sel(SelD));
  Demultiplexer #(.select(3)) demultiplexer_2 (
    .out0(demultiplexer_2_out0), .out1(demultiplexer_2_out1), .out2(demultiplexer_2_out2),
    .out3(demultiplexer_2_out3), .out4(demultiplexer_2_out4), .out5(demultiplexer_2_out5),
    .out6(demultiplexer_2_out6), .out7(demultiplexer_2_out7), .in(W), .sel(SelD));
  Register #(.width(15)) register_1 (
    .D(demultiplexer_1_out0), .en(demultiplexer_2_out0), .clk(CLK), .Q(R0));  // open: clr
  Register #(.width(15)) register_2 (
    .D(demultiplexer_1_out1), .en(demultiplexer_2_out1), .clk(CLK), .Q(R1));  // open: clr
  Register #(.width(15)) register_3 (
    .D(demultiplexer_1_out2), .en(demultiplexer_2_out2), .clk(CLK), .Q(R2));  // open: clr
  Register #(.width(15)) register_4 (
    .D(demultiplexer_1_out3), .en(demultiplexer_2_out3), .clk(CLK), .Q(R3));  // open: clr
  Register #(.width(15)) register_5 (
    .D(demultiplexer_1_out4), .en(demultiplexer_2_out4), .clk(CLK), .Q(R4));  // open: clr
  Register #(.width(15)) register_6 (
    .D(demultiplexer_1_out5), .en(demultiplexer_2_out5), .clk(CLK), .Q(R5));  // open: clr
  Register #(.width(15)) register_7 (
    .D(demultiplexer_1_out6), .en(demultiplexer_2_out6), .clk(CLK), .Q(R6));  // open: clr
  Register #(.width(15)) register_8 (
    .D(demultiplexer_1_out7), .en(demultiplexer_2_out7), .clk(CLK), .Q(register_8_q));  // open: clr
  Multiplexer #(.select(3), .width(15)) multiplexer_1 (
    .in0(R0), .in1(R1), .in2(R2), .in3(R3), .in4(R4), .in5(R5), .in6(R6), .in7(register_8_q), .out(A),
    .sel(SelA));
  Multiplexer #(.select(3), .width(15)) multiplexer_2 (
    .in0(R0), .in1(R1), .in2(R2), .in3(R3), .in4(R4), .in5(R5), .in6(R6), .in7(register_8_q), .out(B),
    .sel(SelB));
endmodule

module ALU15 (
  input  [14:0] A,
  input  [14:0] B,
  input  [2:0] OP,
  input  CIN,
  input  OIN,
  output C,
  output O,
  output N,
  output Z,
  output [14:0] R
);

  wire and_1_out, and_2_out, and_3_out, and_4_out, and_5_out, and_6_out, and_7_out, and_8_out, and_9_out,
       and_10_out, nor_2_out, nor_3_out, nor_4_out, nor_5_out, not_1_out, not_2_out, not_3_out, not_4_out,
       not_5_out, not_6_out, not_7_out, not_8_out, not_9_out, not_10_out, not_11_out, not_12_out, not_13_out,
       not_14_out, not_15_out, or_1_out;
  wire [0:0] controlled_buffer_16_out, controlled_buffer_23_out, controlled_buffer_24_out;
  wire [1:0] controlled_buffer_26_out, controlled_buffer_29_out;
  wire [3:0] controlled_buffer_32_out, controlled_buffer_34_out;
  wire [3:3] controlled_buffer_35_out;
  wire [5:0] controlled_buffer_38_out;
  wire [6:0] controlled_buffer_42_out;
  wire [7:7] controlled_buffer_39_out;
  wire [14:0] adder15_1_s, and_11_out, controlled_buffer_2_out, controlled_buffer_3_out,
       controlled_buffer_4_out, controlled_buffer_5_out, controlled_buffer_6_out, controlled_buffer_7_out,
       controlled_buffer_8_out, controlled_buffer_9_out, controlled_buffer_10_out, controlled_buffer_11_out,
       controlled_buffer_12_out, controlled_buffer_13_out, controlled_buffer_14_out,
       controlled_buffer_15_out, controlled_buffer_21_out, controlled_buffer_22_out,
       controlled_buffer_25_out, controlled_buffer_28_out, controlled_buffer_31_out,
       controlled_buffer_33_out, controlled_buffer_36_out, controlled_buffer_37_out,
       controlled_buffer_40_out, controlled_buffer_41_out, controlled_inverter_1_out, or_2_out, xor_2_out;
  wire [14:1] controlled_buffer_27_out;
  wire [14:13] controlled_buffer_30_out;

  nor nor_1 (Z, R[0], R[1], R[2], R[3], R[4], R[5], R[6], R[7], R[8], R[9], R[10], R[11], R[12], R[13], N);
  xor xor_1 (O, CIN, C);
  nor nor_2 (nor_2_out, OP[1], OP[2]);
  nor nor_3 (nor_3_out, OP[0], OP[1], OP[2]);
  nor nor_4 (nor_4_out, OP[0], OP[2]);
  and and_1 (and_1_out, OP[0], OP[1]);
  nor nor_5 (nor_5_out, OP[0], OP[1]);
  and and_2 (and_2_out, OP[0], OP[2]);
  and and_3 (and_3_out, OP[1], OP[2]);
  and and_4 (and_4_out, OP[0], OP[1], OP[2]);
  and and_5 (and_5_out, OP[0], nor_2_out);
  and and_6 (and_6_out, OP[1], nor_4_out);
  not not_1 (not_1_out, OP[2]);
  and and_7 (and_7_out, OP[2], nor_5_out);
  and and_8 (and_8_out, and_2_out, not_2_out);
  not not_2 (not_2_out, OP[1]);
  and and_9 (and_9_out, and_3_out, not_3_out);
  not not_3 (not_3_out, OP[0]);
  and and_10 (and_10_out, and_1_out, not_1_out);
  assign controlled_inverter_1_out = and_5_out ? ~B : 15'bz;  // Controlled_Inverter controlled_inverter_1
  assign controlled_inverter_1_out = nor_3_out ? B : 15'bz;  // Controlled_Buffer controlled_buffer_1
  or or_1 (or_1_out, nor_3_out, and_5_out);
  assign controlled_buffer_2_out = or_1_out ? A : 15'bz;  // Controlled_Buffer controlled_buffer_2
  assign controlled_buffer_3_out = and_6_out ? B : 15'bz;  // Controlled_Buffer controlled_buffer_3
  assign controlled_buffer_4_out = and_6_out ? A : 15'bz;  // Controlled_Buffer controlled_buffer_4
  assign controlled_buffer_5_out = and_10_out ? B : 15'bz;  // Controlled_Buffer controlled_buffer_5
  assign controlled_buffer_6_out = and_10_out ? A : 15'bz;  // Controlled_Buffer controlled_buffer_6
  assign controlled_buffer_7_out = and_7_out ? B : 15'bz;  // Controlled_Buffer controlled_buffer_7
  assign controlled_buffer_8_out = and_7_out ? A : 15'bz;  // Controlled_Buffer controlled_buffer_8
  assign controlled_buffer_9_out = and_8_out ? B : 15'bz;  // Controlled_Buffer controlled_buffer_9
  assign controlled_buffer_10_out = and_8_out ? A : 15'bz;  // Controlled_Buffer controlled_buffer_10
  assign controlled_buffer_11_out = and_9_out ? B : 15'bz;  // Controlled_Buffer controlled_buffer_11
  assign controlled_buffer_12_out = and_9_out ? A : 15'bz;  // Controlled_Buffer controlled_buffer_12
  assign controlled_buffer_13_out = and_4_out ? B : 15'bz;  // Controlled_Buffer controlled_buffer_13
  assign controlled_buffer_14_out = and_4_out ? A : 15'bz;  // Controlled_Buffer controlled_buffer_14
  assign and_11_out = controlled_buffer_3_out & controlled_buffer_4_out;  // AND_Gate and_11, 15 bits wide
  assign or_2_out = controlled_buffer_5_out | controlled_buffer_6_out;  // OR_Gate or_2, 15 bits wide
  assign xor_2_out = controlled_buffer_7_out ^ controlled_buffer_8_out;  // XOR_Gate xor_2, 15 bits wide
  not not_4 (not_4_out, controlled_buffer_11_out[0]);
  assign controlled_buffer_15_out = not_4_out ? controlled_buffer_12_out : 15'bz;  // Controlled_Buffer controlled_buffer_15
  assign {controlled_buffer_15_out[13:0], controlled_buffer_16_out[0]} = controlled_buffer_11_out[0] ? controlled_buffer_12_out : 15'bz;  // Controlled_Buffer controlled_buffer_16
  not not_5 (not_5_out, controlled_buffer_13_out[0]);
  assign {N, R[13:0]} = or_1_out ? adder15_1_s : 15'bz;  // Controlled_Buffer controlled_buffer_17
  ADDER15 adder15_1 (.A(controlled_buffer_2_out), .B(controlled_inverter_1_out), .CIN(CIN), .COUT(C), .S(adder15_1_s));
  assign {N, R[13:0]} = and_6_out ? and_11_out : 15'bz;  // Controlled_Buffer controlled_buffer_18
  assign {N, R[13:0]} = and_10_out ? or_2_out : 15'bz;  // Controlled_Buffer controlled_buffer_19
  assign {N, R[13:0]} = and_7_out ? xor_2_out : 15'bz;  // Controlled_Buffer controlled_buffer_20
  assign controlled_buffer_21_out = controlled_buffer_9_out[0] ? controlled_buffer_10_out : 15'bz;  // Controlled_Buffer controlled_buffer_21
  assign controlled_buffer_22_out = not_5_out ? controlled_buffer_14_out : 15'bz;  // Controlled_Buffer controlled_buffer_22
  assign {controlled_buffer_22_out[14], controlled_buffer_22_out[12:0], controlled_buffer_23_out[0]} = controlled_buffer_13_out[0] ? controlled_buffer_14_out : 15'bz;  // Controlled_Buffer controlled_buffer_23
  not not_6 (not_6_out, controlled_buffer_9_out[0]);
  assign {controlled_buffer_21_out[13:0], controlled_buffer_24_out[0]} = not_6_out ? controlled_buffer_10_out : 15'bz;  // Controlled_Buffer controlled_buffer_24
  not not_7 (not_7_out, controlled_buffer_11_out[1]);
  assign {{2{controlled_buffer_25_out[14]}}, controlled_buffer_25_out[12:0]} = not_7_out ? controlled_buffer_15_out : 15'bz;  // Controlled_Buffer controlled_buffer_25
  assign {controlled_buffer_25_out[12:0], controlled_buffer_26_out} = controlled_buffer_11_out[1] ? controlled_buffer_15_out : 15'bz;  // Controlled_Buffer controlled_buffer_26
  not not_8 (not_8_out, controlled_buffer_9_out[1]);
  assign {controlled_buffer_27_out, controlled_buffer_27_out[1]} = not_8_out ? {controlled_buffer_21_out[13:0], controlled_buffer_24_out[0]} : 15'bz;  // Controlled_Buffer controlled_buffer_27
  not not_9 (not_9_out, controlled_buffer_13_out[1]);
  assign {controlled_buffer_28_out[14:13], controlled_buffer_28_out[13], controlled_buffer_28_out[11:0]} = not_9_out ? controlled_buffer_22_out : 15'bz;  // Controlled_Buffer controlled_buffer_28
  assign {controlled_buffer_28_out[14], controlled_buffer_28_out[11:0], controlled_buffer_29_out} = controlled_buffer_13_out[1] ? controlled_buffer_22_out : 15'bz;  // Controlled_Buffer controlled_buffer_29
  assign {controlled_buffer_30_out, controlled_buffer_27_out[14:2]} = controlled_buffer_9_out[1] ? {controlled_buffer_21_out[13:0], controlled_buffer_24_out[0]} : 15'bz;  // Controlled_Buffer controlled_buffer_30
  not not_10 (not_10_out, controlled_buffer_11_out[2]);
  assign {{4{controlled_buffer_31_out[14]}}, controlled_buffer_31_out[10:0]} = not_10_out ? {{2{controlled_buffer_25_out[14]}}, controlled_buffer_25_out[12:0]} : 15'bz;  // Controlled_Buffer controlled_buffer_31
  assign {controlled_buffer_31_out[10:0], controlled_buffer_32_out} = controlled_buffer_11_out[2] ? {{2{controlled_buffer_25_out[14]}}, controlled_buffer_25_out[12:0]} : 15'bz;  // Controlled_Buffer controlled_buffer_32
  not not_11 (not_11_out, controlled_buffer_13_out[2]);
  assign {controlled_buffer_33_out[14:13], {3{controlled_buffer_33_out[13]}}, controlled_buffer_33_out[9:0]} = not_11_out ? {controlled_buffer_28_out[14:13], controlled_buffer_28_out[13], controlled_buffer_28_out[11:0]} : 15'bz;  // Controlled_Buffer controlled_buffer_33
  assign {controlled_buffer_33_out[14], controlled_buffer_33_out[9:0], controlled_buffer_34_out} = controlled_buffer_13_out[2] ? {controlled_buffer_28_out[14:13], controlled_buffer_28_out[13], controlled_buffer_28_out[11:0]} : 15'bz;  // Controlled_Buffer controlled_buffer_34
  not not_12 (not_12_out, controlled_buffer_9_out[2]);
  assign {controlled_buffer_36_out[10:0], {4{controlled_buffer_35_out[3]}}} = not_12_out ? {controlled_buffer_27_out, controlled_buffer_27_out[1]} : 15'bz;  // Controlled_Buffer controlled_buffer_35
  assign controlled_buffer_36_out = controlled_buffer_9_out[2] ? {controlled_buffer_27_out, controlled_buffer_27_out[1]} : 15'bz;  // Controlled_Buffer controlled_buffer_36
  not not_13 (not_13_out, controlled_buffer_11_out[3]);
  assign {{6{controlled_buffer_37_out[14]}}, controlled_buffer_37_out[8:0]} = not_13_out ? {{4{controlled_buffer_31_out[14]}}, controlled_buffer_31_out[10:0]} : 15'bz;  // Controlled_Buffer controlled_buffer_37
  assign {controlled_buffer_37_out[8:0], controlled_buffer_38_out} = controlled_buffer_11_out[3] ? {{4{controlled_buffer_31_out[14]}}, controlled_buffer_31_out[10:0]} : 15'bz;  // Controlled_Buffer controlled_buffer_38
  not not_14 (not_14_out, controlled_buffer_9_out[3]);
  assign {controlled_buffer_40_out[6:0], {8{controlled_buffer_39_out[7]}}} = not_14_out ? {controlled_buffer_36_out[10:0], {4{controlled_buffer_35_out[3]}}} : 15'bz;  // Controlled_Buffer controlled_buffer_39
  assign controlled_buffer_40_out = controlled_buffer_9_out[3] ? {controlled_buffer_36_out[10:0], {4{controlled_buffer_35_out[3]}}} : 15'bz;  // Controlled_Buffer controlled_buffer_40
  not not_15 (not_15_out, controlled_buffer_13_out[3]);
  assign {controlled_buffer_41_out[14:13], {6{controlled_buffer_41_out[13]}}, controlled_buffer_41_out[6:0]} = not_15_out ? {controlled_buffer_33_out[14:13], {3{controlled_buffer_33_out[13]}}, controlled_buffer_33_out[9:0]} : 15'bz;  // Controlled_Buffer controlled_buffer_41
  assign {controlled_buffer_41_out[14], controlled_buffer_41_out[6:0], controlled_buffer_42_out} = controlled_buffer_13_out[3] ? {controlled_buffer_33_out[14:13], {3{controlled_buffer_33_out[13]}}, controlled_buffer_33_out[9:0]} : 15'bz;  // Controlled_Buffer controlled_buffer_42
  assign {N, R[13:0]} = and_9_out ? {{6{controlled_buffer_37_out[14]}}, controlled_buffer_37_out[8:0]} : 15'bz;  // Controlled_Buffer controlled_buffer_43
  assign {N, R[13:0]} = and_4_out ? {controlled_buffer_41_out[14:13], {6{controlled_buffer_41_out[13]}}, controlled_buffer_41_out[6:0]} : 15'bz;  // Controlled_Buffer controlled_buffer_44
  assign {N, R[13:0]} = and_8_out ? {controlled_buffer_40_out[6:0], {8{controlled_buffer_39_out[7]}}} : 15'bz;  // Controlled_Buffer controlled_buffer_45

  assign R[14] = N;
  // also tied to GND on the sheet: {controlled_buffer_15_out[14], controlled_buffer_22_out[13], controlled_buffer_21_out[14], controlled_buffer_24_out[0], controlled_buffer_25_out[14], controlled_buffer_28_out[13], controlled_buffer_27_out[1], controlled_buffer_31_out[14], controlled_buffer_33_out[13], controlled_buffer_35_out[3], controlled_buffer_37_out[14], controlled_buffer_41_out[13], controlled_buffer_39_out[7]}
endmodule

module FLAGS8 (
  input  IRQ,
  input  [7:0] NF,
  input  [7:0] WM,
  input  CLK,
  output [7:0] F
);

  wire and_1_out, and_2_out, and_3_out, and_4_out, and_5_out, and_6_out, and_7_out, and_8_out, and_9_out,
       or_1_out, or_2_out;

  and and_1 (and_1_out, F[5], IRQ);
  or or_1 (or_1_out, NF[6], and_1_out);
  or or_2 (or_2_out, and_1_out, WM[6]);
  and and_2 (and_2_out, WM[0], CLK);
  and and_3 (and_3_out, WM[1], CLK);
  and and_4 (and_4_out, WM[2], CLK);
  and and_5 (and_5_out, WM[3], CLK);
  and and_6 (and_6_out, WM[4], CLK);
  and and_7 (and_7_out, WM[5], CLK);
  and and_8 (and_8_out, or_2_out, CLK);
  and and_9 (and_9_out, WM[7], CLK);
  D_Flip_Flop d_ff_1 (.D(NF[0]), .clk(and_2_out), .Q(F[0]));  // open: Qn, preset, reset
  D_Flip_Flop d_ff_2 (.D(NF[1]), .clk(and_3_out), .Q(F[1]));  // open: Qn, preset, reset
  D_Flip_Flop d_ff_3 (.D(NF[2]), .clk(and_4_out), .Q(F[2]));  // open: Qn, preset, reset
  D_Flip_Flop d_ff_4 (.D(NF[3]), .clk(and_5_out), .Q(F[3]));  // open: Qn, preset, reset
  D_Flip_Flop d_ff_5 (.D(NF[4]), .clk(and_6_out), .Q(F[4]));  // open: Qn, preset, reset
  D_Flip_Flop d_ff_6 (.D(NF[5]), .clk(and_7_out), .Q(F[5]));  // open: Qn, preset, reset
  D_Flip_Flop d_ff_7 (.D(or_1_out), .clk(and_8_out), .Q(F[6]));  // open: Qn, preset, reset
  D_Flip_Flop d_ff_8 (.D(NF[7]), .clk(and_9_out), .Q(F[7]));  // open: Qn, preset, reset
endmodule

module IMM15 (
  input  [14:0] INST,
  output [14:0] SEXT
);

  wire [14:0] multiplexer_1_out;

  Multiplexer #(.select(3), .width(15)) multiplexer_1 (
    .in3({{12{INST[14]}}, INST[13:11]}), .in4({{9{INST[14]}}, INST[13:8]}),
    .in5({{9{INST[14]}}, INST[13:8]}), .in6({{12{INST[14]}}, INST[7:5]}),
    .in7({{5{INST[14]}}, INST[13:8], 4'b0000}), .out(multiplexer_1_out), .sel(INST[2:0]));  // open: in0, in1, in2
  Multiplexer #(.select(2), .width(15)) multiplexer_2 (
    .in0({15{1'b0}}), .in1({{12{INST[14]}}, INST[13:11]}), .in2({{6{INST[14]}}, INST[13:5]}),
    .in3(multiplexer_1_out), .out(SEXT), .sel(INST[4:3]));
endmodule

module DECODE15 (
  input  [4:0] OPCODE,
  output SWI,
  output STORE,
  output LOAD,
  output [1:0] ASEL,
  output [1:0] BSEL,
  output [2:0] ALUOP,
  output [2:0] REGDATASRC,
  output REGW,
  output [1:0] FLAGSRC,
  output [7:0] FLAGWM,
  output SRPW,
  output SRFW
);

  wire not_1_out, not_2_out, not_3_out, not_4_out, not_5_out;

  ROM #(.addrWidth(5), .dataWidth(2)) rom_1 (.addr(OPCODE), .data(ASEL));
  ROM #(.addrWidth(5), .dataWidth(2)) rom_2 (.addr(OPCODE), .data(BSEL));
  ROM #(.addrWidth(5), .dataWidth(3)) rom_3 (.addr(OPCODE), .data(ALUOP));
  ROM #(.addrWidth(5), .dataWidth(3)) rom_4 (.addr(OPCODE), .data(REGDATASRC));
  ROM #(.addrWidth(5), .dataWidth(1)) rom_5 (.addr(OPCODE), .data(REGW));
  ROM #(.addrWidth(5), .dataWidth(2)) rom_6 (.addr(OPCODE), .data(FLAGSRC));
  ROM #(.addrWidth(5)) rom_7 (.addr(OPCODE), .data(FLAGWM));
  ROM #(.addrWidth(5), .dataWidth(1)) rom_8 (.addr(OPCODE), .data(SRPW));
  ROM #(.addrWidth(5), .dataWidth(1)) rom_9 (.addr(OPCODE), .data(SRFW));
  not not_1 (not_1_out, OPCODE[3]);
  not not_2 (not_2_out, OPCODE[0]);
  not not_3 (not_3_out, OPCODE[2]);
  not not_4 (not_4_out, OPCODE[4]);
  and and_1 (SWI, OPCODE[0], OPCODE[1], OPCODE[2], not_1_out, OPCODE[4]);
  and and_2 (STORE, not_2_out, OPCODE[1], OPCODE[2], OPCODE[3], OPCODE[4]);
  not not_5 (not_5_out, OPCODE[1]);
  and and_3 (LOAD, OPCODE[0], not_5_out, not_3_out, OPCODE[3], not_4_out);
endmodule
